// Logisim project 1位ALU-最低位.circ as structural Verilog: 1 circuit, main circuit main
module main (
  input  Binvert,
  input  [1:0] Operation,
  input  a,
  input  b,
  output Result,
  output CarryOut
);

  wire adder_1_out, and_1_out, multiplexer_1_out, not_1_out, or_1_out;

  not not_1 (not_1_out, b);
  Multiplexer multiplexer_1 (.in0(b), .in1(not_1_out), .out(multiplexer_1_out), .sel(Binvert));  // open: en
  and and_1 (and_1_out, a, multiplexer_1_out);
  or or_1 (or_1_out, a, multiplexer_1_out);
  Adder #(.width(1)) adder_1 (.a(a), .b(multiplexer_1_out), .out(adder_1_out), .cin(Binvert), .cout(CarryOut));
  Multiplexer #(.select(2)) multiplexer_2 (
    .in0(and_1_out), .in1(or_1_out), .in2(adder_1_out), .out(Result), .sel(Operation));  // open: in3, en
endmodule
