// Logisim project 8位ALU.circ as structural Verilog: 3 circuits, main circuit main
module main (
  input  Binvert,
  input  [1:0] Operation,
  input  a,
  input  b,
  output Result,
  output CarryOut
);

  wire adder_1_out, and_1_out, multiplexer_1_out, not_1_out, or_1_out;

  not not_1 (not_1_out, b);
  Multiplexer multiplexer_1 (.in0(b), .in1(not_1_out), .out(multiplexer_1_out), .sel(Binvert));  // open: en
  and and_1 (and_1_out, a, multiplexer_1_out);
  or or_1 (or_1_out, a, multiplexer_1_out);
  Adder #(.width(1)) adder_1 (.a(a), .b(multiplexer_1_out), .out(adder_1_out), .cin(Binvert), .cout(CarryOut));
  Multiplexer #(.select(2)) multiplexer_2 (
    .in0(and_1_out), .in1(or_1_out), .in2(adder_1_out), .out(Result), .sel(Operation));  // open: in3, en
endmodule

module main2 (
  input  Binvert,
  input  CarryIn,
  input  [1:0] in_3,
  input  a,
  input  b,
  output Result,
  output CarryIn_2
);

  wire adder_1_out, and_1_out, multiplexer_1_out, not_1_out, or_1_out;

  not not_1 (not_1_out, b);
  Multiplexer multiplexer_1 (.in0(b), .in1(not_1_out), .out(multiplexer_1_out), .sel(Binvert));  // open: en
  and and_1 (and_1_out, a, multiplexer_1_out);
  or or_1 (or_1_out, a, multiplexer_1_out);
  Adder #(.width(1)) adder_1 (.a(a), .b(multiplexer_1_out), .out(adder_1_out), .cin(CarryIn), .cout(CarryIn_2));
  Multiplexer #(.select(2)) multiplexer_2 (
    .in0(and_1_out), .in1(or_1_out), .in2(adder_1_out), .out(Result), .sel(in_3));  // open: in3, en
endmodule

module composition (
  input  Binvert,
  input  [1:0] in_2,
  input  A0,
  input  B0,
  input  A1,
  input  B1,
  input  A2,
  input  B2,
  input  A3,
  input  B3,
  input  A4,
  input  B4,
  input  A5,
  input  B5,
  input  A6,
  input  B6,
  input  A7,
  input  B7,
  output S0,
  output S1,
  output S2,
  output S3,
  output S4,
  output S5,
  output S6,
  output S7,
  output CarryIn
);

  wire main2_1_carryin_2, main2_2_carryin_2, main2_3_carryin_2, main2_4_carryin_2, main2_5_carryin_2,
       main2_6_carryin_2, main_1_carryout;

  main main_1 (.Operation(in_2), .a(A0), .b(B0), .Binvert(Binvert), .CarryOut(main_1_carryout), .Result(S0));
  main2 main2_1 (
    .in_3(in_2), .a(A1), .b(B1), .Result(S1), .CarryIn_2(main2_1_carryin_2), .Binvert(Binvert),
    .CarryIn(main_1_carryout));
  main2 main2_2 (
    .in_3(in_2), .a(A2), .b(B2), .Result(S2), .CarryIn_2(main2_2_carryin_2), .Binvert(Binvert),
    .CarryIn(main2_1_carryin_2));
  main2 main2_3 (
    .in_3(in_2), .a(A3), .b(B3), .Result(S3), .CarryIn_2(main2_3_carryin_2), .Binvert(Binvert),
    .CarryIn(main2_2_carryin_2));
  main2 main2_4 (
    .in_3(in_2), .a(A4), .b(B4), .Result(S4), .CarryIn_2(main2_4_carryin_2), .Binvert(Binvert),
    .CarryIn(main2_3_carryin_2));
  main2 main2_5 (
    .in_3(in_2), .a(A5), .b(B5), .Result(S5), .CarryIn_2(main2_5_carryin_2), .Binvert(Binvert),
    .CarryIn(main2_4_carryin_2));
  main2 main2_6 (
    .in_3(in_2), .a(A6), .b(B6), .Result(S6), .CarryIn_2(main2_6_carryin_2), .Binvert(Binvert),
    .CarryIn(main2_5_carryin_2));
  main2 main2_7 (
    .in_3(in_2), .a(A7), .b(B7), .Result(S7), .CarryIn_2(CarryIn), .Binvert(Binvert),
    .CarryIn(main2_6_carryin_2));
endmodule
