// Logisim project temp.circ as structural Verilog: 7 circuits, main circuit main
module main (
  input  Binvert,
  input  [1:0] in_2,
  input  a,
  input  b,
  output out_5,
  output out_6
);

  wire adder_1_out, and_1_out, multiplexer_1_out, not_1_out, or_1_out;

  not not_1 (not_1_out, b);
  Multiplexer multiplexer_1 (.in0(b), .in1(not_1_out), .out(multiplexer_1_out), .sel(Binvert));  // open: en
  and and_1 (and_1_out, a, multiplexer_1_out);
  or or_1 (or_1_out, a, multiplexer_1_out);
  Adder #(.width(1)) adder_1 (.a(a), .b(multiplexer_1_out), .out(adder_1_out), .cin(Binvert), .cout(out_6));
  Multiplexer #(.select(2)) multiplexer_2 (
    .in0(and_1_out), .in1(or_1_out), .in2(adder_1_out), .out(out_5), .sel(in_2));  // open: in3, en
endmodule

module circuit1 (
  input  in_1,
  input  in_2,
  input  in_3,
  input  in_4,
  input  in_5,
  input  in_6,
  input  in_7,
  input  in_8,
  input  in_9,
  input  in_10,
  input  in_11,
  input  in_12,
  input  in_13,
  input  in_14,
  input  in_15,
  input  in_16,
  input  in_17,
  output out_18,
  output out_19,
  output out_20,
  output out_21,
  output out_22,
  output out_23,
  output out_24,
  output out_25
);

  wire and_1_out, and_2_out, and_3_out, and_4_out, and_5_out, and_6_out, and_7_out, and_8_out, or_1_out,
       or_2_out, or_3_out, or_4_out, or_5_out, or_6_out, or_7_out, or_8_out, undriven;

  and and_1 (and_1_out, in_1, in_2);
  and and_2 (and_2_out, in_3, in_4);
  and and_3 (and_3_out, in_5, in_6);
  and and_4 (and_4_out, in_7, in_8);
  and and_5 (and_5_out, in_9, in_10);
  and and_6 (and_6_out, in_11, in_12);
  and and_7 (and_7_out, in_13, in_14);
  and and_8 (and_8_out, in_15, in_16);
  or or_1 (or_1_out, in_1, in_2);
  or or_2 (or_2_out, in_3, in_4);
  or or_3 (or_3_out, in_5, in_6);
  or or_4 (or_4_out, in_7, in_8);
  or or_5 (or_5_out, in_9, in_10);
  or or_6 (or_6_out, in_11, in_12);
  or or_7 (or_7_out, in_13, in_14);
  or or_8 (or_8_out, in_15, in_16);
  Multiplexer multiplexer_1 (.in0(or_1_out), .in1(and_1_out), .out(out_18), .sel(in_17), .en(undriven));
  Multiplexer multiplexer_2 (.in0(or_2_out), .in1(and_2_out), .out(out_19), .sel(in_17));  // open: en
  Multiplexer multiplexer_3 (.in0(or_3_out), .in1(and_3_out), .out(out_20), .sel(in_17));  // open: en
  Multiplexer multiplexer_4 (.in0(or_4_out), .in1(and_4_out), .out(out_21), .sel(in_17));  // open: en
  Multiplexer multiplexer_5 (.in0(or_5_out), .in1(and_5_out), .out(out_22), .sel(in_17));  // open: en
  Multiplexer multiplexer_6 (.in0(or_6_out), .in1(and_6_out), .out(out_23), .sel(in_17));  // open: en
  Multiplexer multiplexer_7 (.in0(or_7_out), .in1(and_7_out), .out(out_24), .sel(in_17));  // open: en
  Multiplexer multiplexer_8 (.in0(or_8_out), .in1(and_8_out), .out(out_25), .sel(in_17));  // open: en
endmodule

module circuit2 (
  input  B7,
  input  B6,
  input  B5,
  input  B4,
  input  B3,
  input  B2,
  input  B1,
  input  B0,
  input  A7,
  input  A6,
  input  A5,
  input  A4,
  input  A3,
  input  A2,
  input  A1,
  input  A0,
  input  in_17,
  output Overflow,
  output out_19,
  output S7,
  output S6,
  output S5,
  output S4,
  output S2,
  output S1,
  output S0,
  output out_27
);

  wire test_2_out_5, test_3_out_5, test_4_out_5, test_5_out_5, test_6_out_5, test_7_out_5, test_8_out_5,
       xor_2_out, xor_3_out, xor_4_out, xor_5_out, xor_6_out, xor_7_out, xor_8_out, xor_9_out;

  xor xor_1 (Overflow, test_2_out_5, out_27);
  xor xor_2 (xor_2_out, in_17, B7);
  test test_1 (.in_2(A7), .in_3(xor_2_out), .in_1(test_2_out_5), .out_5(out_27), .out_4(S7));
  test test_2 (.in_2(A6), .in_3(xor_3_out), .in_1(test_3_out_5), .out_5(test_2_out_5), .out_4(S6));
  xor xor_3 (xor_3_out, in_17, B6);
  test test_3 (.in_2(A5), .in_3(xor_4_out), .in_1(test_4_out_5), .out_5(test_3_out_5), .out_4(S5));
  xor xor_4 (xor_4_out, in_17, B5);
  test test_4 (.in_2(A4), .in_3(xor_5_out), .in_1(test_5_out_5), .out_5(test_4_out_5), .out_4(S4));
  xor xor_5 (xor_5_out, in_17, B4);
  test test_5 (.in_2(A3), .in_3(xor_6_out), .in_1(test_6_out_5), .out_5(test_5_out_5), .out_4(out_19));
  xor xor_6 (xor_6_out, in_17, B3);
  xor xor_7 (xor_7_out, in_17, B2);
  test test_6 (.in_2(A2), .in_3(xor_7_out), .in_1(test_7_out_5), .out_5(test_6_out_5), .out_4(S2));
  test test_7 (.in_2(A1), .in_3(xor_8_out), .in_1(test_8_out_5), .out_5(test_7_out_5), .out_4(S1));
  xor xor_8 (xor_8_out, in_17, B1);
  test test_8 (.in_2(A0), .in_3(xor_9_out), .in_1(in_17), .out_5(test_8_out_5), .out_4(S0));
  xor xor_9 (xor_9_out, in_17, B0);
endmodule

module circuit3 (
  input  in_1,
  input  in_2,
  input  in_3,
  input  in_4,
  input  in_5,
  input  in_6,
  input  in_7,
  input  in_8,
  input  in_9,
  input  in_10,
  input  in_11,
  input  in_12,
  input  in_13,
  input  in_14,
  input  in_15,
  input  in_16,
  input  in_17,
  output out_18,
  output out_19,
  output out_20,
  output out_21,
  output out_22,
  output out_23,
  output out_24,
  output out_25,
  output out_26
);

  wire or_1_out, or_2_out, or_3_out, or_4_out, or_5_out, or_6_out;

  Multiplexer multiplexer_1 (.in0(in_1), .in1(in_2), .out(out_18), .sel(in_17));  // open: en
  Multiplexer multiplexer_2 (.in0(in_3), .in1(in_4), .out(out_19), .sel(in_17));  // open: en
  Multiplexer multiplexer_3 (.in0(in_5), .out(out_20), .sel(in_17));  // open: in1, en
  Multiplexer multiplexer_4 (.in0(in_7), .in1(in_8), .out(out_21), .sel(in_17));  // open: en
  Multiplexer multiplexer_5 (.in0(in_9), .in1(in_10), .out(out_23), .sel(in_17));  // open: en
  Multiplexer multiplexer_6 (.in0(in_11), .in1(in_12), .out(out_24), .sel(in_17));  // open: en
  Multiplexer multiplexer_7 (.in0(in_13), .in1(in_14), .out(out_25), .sel(in_17));  // open: en
  Multiplexer multiplexer_8 (.in0(in_15), .in1(in_16), .out(out_26), .sel(in_17));  // open: en
  or or_1 (or_1_out, out_18, out_19);
  or or_2 (or_2_out, out_20, out_21);
  or or_3 (or_3_out, out_23, out_24);
  or or_4 (or_4_out, out_25, out_26);
  or or_5 (or_5_out, or_1_out, or_2_out);
  or or_6 (or_6_out, or_3_out, or_4_out);
  or or_7 (out_22, or_5_out, or_6_out);
endmodule

module total (
  input  in_1,
  input  in_2,
  input  in_3,
  input  in_4,
  input  in_5,
  input  in_6,
  input  in_7,
  input  in_8,
  input  in_9,
  input  in_10,
  input  in_11,
  input  in_12,
  input  in_13,
  input  in_14,
  input  in_15,
  input  in_16,
  input  in_17,
  input  in_18
);

  wire circuit1_1_out_19, circuit1_1_out_20, circuit1_1_out_21, circuit2_1_p1, circuit2_1_p2, circuit2_1_p7,
       circuit2_1_p9, circuit2_1_p11, circuit2_1_p13, circuit2_1_p15, circuit2_1_p17, circuit2_1_p19,
       circuit2_1_p21, circuit3_1_out_18, circuit3_1_out_19, circuit3_1_out_20, circuit3_1_out_21,
       circuit3_1_out_22, circuit3_1_out_23, circuit3_1_out_24, circuit3_1_out_25, circuit3_1_out_26,
       undriven, undriven_2, undriven_3, undriven_4, undriven_5;

  circuit1 circuit1_1 (
    .in_3(undriven), .out_19(circuit1_1_out_19), .in_4(undriven_2), .in_5(undriven_3),
    .out_20(circuit1_1_out_20), .in_6(undriven_4), .in_7(undriven_5), .out_21(circuit1_1_out_21));  // open: in_1, out_18, in_2, in_8, in_9, out_22, in_10, in_11, out_23, in_12, in_13, out_24, in_14, in_15, out_25, in_16, in_17
  // circuit2 circuit2_1: pin names not known; wires that end beside it: circuit2_1_p1, circuit2_1_p2, in_1, in_2, in_3, in_4, circuit2_1_p7, in_5, circuit2_1_p9, in_6, circuit2_1_p11, in_7, circuit2_1_p13, in_8, circuit2_1_p15, in_9, circuit2_1_p17, in_10, circuit2_1_p19, in_11, circuit2_1_p21, in_12, in_13, in_14, in_15, in_16, in_18
  circuit3 circuit3_1 (
    .in_1(circuit2_1_p13), .in_2(circuit2_1_p15), .in_3(circuit2_1_p17), .in_4(circuit2_1_p19),
    .in_5(circuit2_1_p21), .in_6(undriven), .in_7(circuit1_1_out_19), .in_8(undriven_2), .in_9(undriven_3),
    .in_10(circuit1_1_out_20), .in_11(undriven_4), .in_12(undriven_5), .in_13(circuit1_1_out_21),
    .in_14(circuit2_1_p11), .in_15(circuit2_1_p9), .in_16(circuit2_1_p7), .out_18(circuit3_1_out_18),
    .out_19(circuit3_1_out_19), .out_20(circuit3_1_out_20), .out_21(circuit3_1_out_21),
    .out_23(circuit3_1_out_23), .out_24(circuit3_1_out_24), .out_25(circuit3_1_out_25),
    .out_26(circuit3_1_out_26), .in_17(in_17), .out_22(circuit3_1_out_22));
endmodule

module test (
  input  in_1,
  input  in_2,
  input  in_3,
  output out_4,
  output out_5
);

  wire and_1_out, and_2_out, and_3_out, and_4_out, and_5_out, and_6_out, and_7_out, not_1_out, not_2_out,
       not_3_out;

  not not_1 (not_1_out, in_2);
  not not_2 (not_2_out, in_3);
  not not_3 (not_3_out, in_1);
  and and_1 (and_1_out, in_2, not_2_out, not_3_out);
  and and_2 (and_2_out, not_1_out, in_3, not_3_out);
  and and_3 (and_3_out, not_1_out, not_2_out, in_1);
  and and_4 (and_4_out, in_2, in_3, in_1);
  and and_5 (and_5_out, in_1, in_2);
  and and_6 (and_6_out, in_1, in_3);
  and and_7 (and_7_out, in_2, in_3);
  or or_1 (out_5, and_5_out, and_6_out, and_7_out);
  or or_2 (out_4, and_1_out, and_2_out, and_3_out, and_4_out);
endmodule

module \or  (
  input  A7,
  input  B7,
  input  A6,
  input  B6,
  input  A5,
  input  B5,
  input  A4,
  input  B4,
  input  A3,
  input  B3,
  input  A2,
  input  B2,
  input  A1,
  input  B1,
  input  A0,
  input  B0,
  input  in_17,
  output out_18,
  output out_19,
  output out_20,
  output out_21,
  output out_22,
  output out_23,
  output out_24,
  output out_25
);

  wire and_1_out, and_2_out, and_3_out, and_4_out, and_5_out, and_6_out, and_7_out, and_8_out, or_1_out,
       or_2_out, or_3_out, or_4_out, or_5_out, or_6_out, or_7_out, or_8_out, undriven;

  and and_1 (and_1_out, A7, B7);
  and and_2 (and_2_out, A6, B6);
  and and_3 (and_3_out, A5, B5);
  and and_4 (and_4_out, A4, B4);
  and and_5 (and_5_out, A3, B3);
  and and_6 (and_6_out, A2, B2);
  and and_7 (and_7_out, A1, B1);
  and and_8 (and_8_out, A0, B0);
  or or_1 (or_1_out, A7, B7);
  or or_2 (or_2_out, A6, B6);
  or or_3 (or_3_out, A5, B5);
  or or_4 (or_4_out, A4, B4);
  or or_5 (or_5_out, A3, B3);
  or or_6 (or_6_out, A2, B2);
  or or_7 (or_7_out, A1, B1);
  or or_8 (or_8_out, A0, B0);
  Multiplexer multiplexer_1 (.in0(or_1_out), .in1(and_1_out), .out(out_18), .sel(in_17), .en(undriven));
  Multiplexer multiplexer_2 (.in0(or_2_out), .in1(and_2_out), .out(out_19), .sel(in_17));  // open: en
  Multiplexer multiplexer_3 (.in0(or_3_out), .in1(and_3_out), .out(out_20), .sel(in_17));  // open: en
  Multiplexer multiplexer_4 (.in0(or_4_out), .in1(and_4_out), .out(out_21), .sel(in_17));  // open: en
  Multiplexer multiplexer_5 (.in0(or_5_out), .in1(and_5_out), .out(out_22), .sel(in_17));  // open: en
  Multiplexer multiplexer_6 (.in0(or_6_out), .in1(and_6_out), .out(out_23), .sel(in_17));  // open: en
  Multiplexer multiplexer_7 (.in0(or_7_out), .in1(and_7_out), .out(out_24), .sel(in_17));  // open: en
  Multiplexer multiplexer_8 (.in0(or_8_out), .in1(and_8_out), .out(out_25), .sel(in_17));  // open: en
endmodule
